// Logisim project Q1.circ as structural Verilog: 1 circuit, main circuit main
module main (
);

  wire D0_out, D1_out, D2_out, D3_out, D4_out, D5_out, D6_out, D7_out, X_out, X_prime_out, Y_out,
       Y_prime_out, Z_out, Z_prime_out;

  Button X (.out(X_out));
  Button Y (.out(Y_out));
  not X_prime (X_prime_out, X_out);
  not Y_prime (Y_prime_out, Y_out);
  Button Z (.out(Z_out));
  not Z_prime (Z_prime_out, Z_out);
  and D0 (D0_out, Z_prime_out, Y_prime_out, X_prime_out);
  and D1 (D1_out, Z_out, Y_prime_out, X_prime_out);
  and D2 (D2_out, Z_prime_out, Y_out, X_prime_out);
  and D3 (D3_out, Z_out, Y_out, X_prime_out);
  and D4 (D4_out, Z_prime_out, Y_prime_out, X_out);
  and D5 (D5_out, Z_out, Y_prime_out, X_out);
  and D6 (D6_out, Z_prime_out, Y_out, X_out);
  and D7 (D7_out, Z_out, Y_out, X_out);
  LED _0 (.in(D0_out));
  LED _1 (.in(D1_out));
  LED _2 (.in(D2_out));
  LED _3 (.in(D3_out));
  LED _4 (.in(D4_out));
  LED _5 (.in(D5_out));
  LED _6 (.in(D6_out));
  LED _7 (.in(D7_out));
endmodule
