// Logisim project Q2.circ as structural Verilog: 1 circuit, main circuit main
module main (
);

  wire A_out, A_prime_out, and_1_out, B_out, C_out, or_1_out, xor_1_out;

  Button A (.out(A_out));
  Button B (.out(B_out));
  Button C (.out(C_out));
  not A_prime (A_prime_out, A_out);
  and and_1 (and_1_out, A_prime_out, B_out);
  or or_1 (or_1_out, A_out, C_out);
  xor xor_1 (xor_1_out, and_1_out, or_1_out);
  LED led_1 (.in(xor_1_out));
endmodule
