// Logisim project Q3.circ as structural Verilog: 1 circuit, main circuit main
module main (
);

  wire and_1_out, not_1_out, not_2_out, not_3_out, not_4_out, not_5_out, not_6_out, or_1_out, or_2_out,
       or_3_out, or_4_out, X_out, Y_out, Z_out;

  Button X (.out(X_out));
  Button Y (.out(Y_out));
  Button Z (.out(Z_out));
  not not_1 (not_1_out, Z_out);
  not not_2 (not_2_out, Y_out);
  not not_3 (not_3_out, X_out);
  not not_4 (not_4_out, X_out);
  not not_5 (not_5_out, Y_out);
  not not_6 (not_6_out, Z_out);
  or or_1 (or_1_out, X_out, Y_out, not_1_out);
  or or_2 (or_2_out, X_out, not_2_out, Z_out);
  or or_3 (or_3_out, not_3_out, Y_out, Z_out);
  or or_4 (or_4_out, not_4_out, not_5_out, not_6_out);
  and and_1 (and_1_out, or_1_out, or_2_out, or_3_out, or_4_out);
  LED led_1 (.in(and_1_out));
endmodule
