// Logisim project Q4.circ as structural Verilog: 1 circuit, main circuit main
module main (
);

  wire and_1_out, and_2_out, m_out, m_prime_out, or_1_out, w_out, w_prime_out;

  Button m (.out(m_out));
  Button w (.out(w_out));
  not m_prime (m_prime_out, m_out);
  not w_prime (w_prime_out, w_out);
  and and_1 (and_1_out, w_out, m_prime_out);
  and and_2 (and_2_out, w_prime_out, m_out);
  or or_1 (or_1_out, and_1_out, and_2_out);
  LED K (.in(or_1_out));

  // Notes on the sheet:
  //    K=m'w+mw'
endmodule
