// Logisim project Q6.circ as structural Verilog: 1 circuit, main circuit main
module main (
);

  wire A_out, and_1_out, and_2_out, and_3_out, and_4_out, and_5_out, B_out, C_out, not_1_out, or_1_out,
       or_2_out, or_3_out;

  Button A (.out(A_out));
  Button B (.out(B_out));
  Button C (.out(C_out));
  and and_1 (and_1_out, A_out, B_out, C_out);
  or or_1 (or_1_out, A_out, B_out, C_out);
  and and_2 (and_2_out, A_out, B_out);
  and and_3 (and_3_out, A_out, C_out);
  and and_4 (and_4_out, B_out, C_out);
  or or_2 (or_2_out, and_2_out, and_3_out, and_4_out);
  not not_1 (not_1_out, or_2_out);
  and and_5 (and_5_out, or_1_out, not_1_out);
  LED F1 (.in(or_3_out));
  or or_3 (or_3_out, and_1_out, and_5_out);
  LED F2 (.in(or_2_out));
endmodule
